# Fritzing sketch GreenpowerDatalogger (saved by Fritzing 0.9.3b)
breadboards: 1

parts:
  Part2 = Adafruit Datalogger Shield v1 [part_number="Adafruit #1141"]
  R2 = Resistor [tolerance=±5% resistance=10k package=THT]
  R3 = Resistor [tolerance=±5% resistance=10k package=THT]
  R4 = Resistor [tolerance=±5% resistance=10k package=THT]
  R5 = Resistor [tolerance=±5% resistance=10k package=THT]
  R7 = Resistor [tolerance=±5% resistance=10k package=THT]
  R8 = Resistor [tolerance=±5% resistance=10k package=THT]
  LCD1 = LCD screen
  R9 = Resistor [tolerance=±5% resistance=10k package=THT]
  CURRENT_SENSOR1 = CURRENT SENSOR ACS758
  Q1 = PNP-Transistor [package="TO92 [THT]"]
  VCC1 = Battery

nets:
  N1: Part2.D2, R8.Pin_0, Q1.C
  GND: Part2.GND, Part2.N$54, R7.Pin_1, LCD1.VSS, LCD1.V0, CURRENT_SENSOR1.GND, Q1.B, VCC1.-
  +5V: Part2.+5V, Part2.N$11, R8.Pin_1, CURRENT_SENSOR1.VCC, Q1.E
  N2: Part2.A1, Part2.N$106, R2.Pin_0
  N3: Part2.A2, CURRENT_SENSOR1.VIOUT
  N4: Part2.VIN, VCC1.+
  N5: Part2.N$39, R4.Pin_1, R5.Pin_1
  N6: Part2.N$50, R9.Pin_1
  N7: Part2.N$57, R5.Pin_0, R9.Pin_0
  N8: Part2.N$62, R2.Pin_1, R3.Pin_1
  N9: Part2.N$70, R3.Pin_0, R4.Pin_0
  N10: Part2.N$93, R7.Pin_0

notes:
  Battery +
  Battery -
  Current -
  Current +
  Magnet sensor for speed (dot on top)

custom parts:
  Adafruit Datalogger Shield v1: Here's a handy Arduino shield: we've had a lot of people looking for a dedicated and well-designed data logging shield. We worked hard to engineer an inexpensive but well-rounded design. Not only is it easy to assemble and customize, it also comes with great documentation and libraries. New! we now are carrying an 'assembled' version of this shield, with all the components pre-soldered. NOTE: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
  CURRENT SENSOR ACS758: CURRENT SENSOR
